# Fritzing sketch Breadboard layout (saved by Fritzing 0.9.3b)
breadboards: 6

parts:
  DI1 = 7-Segment LED Display [package=THT]
  DI2 = 7-Segment LED Display [package=THT]
  Part1 = Arduino Nano (Rev3.0) (ICSP)
  SW1 = DIP Switch 8 Position [package=dipswitch-08]
  SW2 = DIP Switch 8 Position [package=dipswitch-08]
  SW3 = DIP Switch 8 Position [package=dipswitch-08]
  IC2 = IC, DIP package, 16 pins [chip_label=74LS48]
  IC7 = IC, DIP package, 16 pins [chip_label=74LS48]
  IC5 = IC, DIP package, 16 pins [chip_label=74LS165]
  IC8 = IC, DIP package, 16 pins [chip_label=74LS165]
  IC9 = IC, DIP package, 16 pins [chip_label=74LS165]
  R1 = Resistor [tolerance=±5% resistance=220 package="0402 [SMD]"]
  R2 = Resistor [tolerance=±5% resistance=220 package="0402 [SMD]"]  # not connected
  R3 = Resistor [tolerance=±5% resistance=220 package="0402 [SMD]"]
  R4 = Resistor [tolerance=±5% resistance=220 package="0402 [SMD]"]  # not connected
  R5 = Resistor [tolerance=±5% resistance=220 package="0402 [SMD]"]  # not connected
  R6 = Resistor [tolerance=±5% resistance=220 package="0402 [SMD]"]
  R7 = Resistor [tolerance=±5% resistance=220 package="0402 [SMD]"]  # not connected
  R8 = Resistor [tolerance=±5% resistance=220 package="0402 [SMD]"]
  R9 = Resistor [tolerance=±5% resistance=220 package="0402 [SMD]"]
  R10 = Resistor [tolerance=±5% resistance=220 package="0402 [SMD]"]
  R11 = Resistor [tolerance=±5% resistance=220 package="0402 [SMD]"]  # not connected
  R12 = Resistor [tolerance=±5% resistance=220 package="0402 [SMD]"]  # not connected
  R13 = Resistor [tolerance=±5% resistance=220 package="0402 [SMD]"]  # not connected
  R14 = Resistor [tolerance=±5% resistance=220 package="0402 [SMD]"]  # not connected
  R15 = Resistor [tolerance=±5% resistance=10k package=THT]
  R16 = Resistor [tolerance=±5% resistance=10k package=THT]
  R17 = Resistor [tolerance=±5% resistance=10k package=THT]
  R18 = Resistor [tolerance=±5% resistance=10k package=THT]
  R19 = Resistor [tolerance=±5% resistance=10k package=THT]
  R20 = Resistor [tolerance=±5% resistance=10k package=THT]
  R21 = Resistor [tolerance=±5% resistance=10k package=THT]
  R22 = Resistor [tolerance=±5% resistance=10k package=THT]
  R23 = Resistor [tolerance=±5% resistance=10k package=THT]
  R24 = Resistor [tolerance=±5% resistance=10k package=THT]
  R25 = Resistor [tolerance=±5% resistance=10k package=THT]
  R26 = Resistor [tolerance=±5% resistance=10k package=THT]
  R27 = Resistor [tolerance=±5% resistance=10k package=THT]
  R28 = Resistor [tolerance=±5% resistance=10k package=THT]
  R29 = Resistor [tolerance=±5% resistance=10k package=THT]
  R30 = Resistor [tolerance=±5% resistance=10k package=THT]
  R31 = Resistor [tolerance=±5% resistance=10k package=THT]
  R32 = Resistor [tolerance=±5% resistance=10k package=THT]
  R33 = Resistor [tolerance=±5% resistance=10k package=THT]
  R34 = Resistor [tolerance=±5% resistance=10k package=THT]
  R35 = Resistor [tolerance=±5% resistance=10k package=THT]
  R36 = Resistor [tolerance=±5% resistance=10k package=THT]
  R37 = Resistor [tolerance=±5% resistance=10k package=THT]
  R38 = Resistor [tolerance=±5% resistance=10k package=THT]
  IC10 = IC, DIP package, 16 pins [chip_label=74HC595]

nets:
  N1: DI1.cathodeE, R6.Pin_1
  N2: DI1.commAnode#7, DI2.commAnode#7, SW1.9, SW1.10, SW1.11, SW1.12, SW1.13, SW1.14, SW1.15, SW1.16, SW2.9, SW2.10, SW2.11, SW2.12, SW2.13, SW2.14, SW2.15, SW2.16, SW3.9, SW3.10, SW3.11, SW3.12, SW3.13, SW3.14, SW3.15, SW3.16, IC2.pin16, IC7.pin16
  N3: DI2.cathodeE, R1.Pin_1
  N4: DI2.cathodeC, R3.Pin_1
  N5: DI2.cathodeA, R8.Pin_0
  N6: DI2.cathodeF, R9.Pin_0
  N7: Part1.D2, IC5.pin2, IC8.pin2, IC9.pin2
  N8: Part1.D5, IC10.pin14
  N9: Part1.D6, IC2.pin4, IC7.pin4
  N10: Part1.D7, IC8.pin7
  N11: Part1.D8, IC10.pin12
  N12: Part1.D9, IC9.pin7
  N13: Part1.D10, IC5.pin15, IC8.pin15, IC9.pin15
  N14: Part1.D11/MOSI, IC5.pin7
  N15: Part1.D12/MISO, IC5.pin1, IC8.pin1, IC9.pin1
  N16: SW1.1, IC5.pin6
  N17: SW1.2, IC5.pin5
  N18: SW1.3, IC5.pin4
  N19: SW1.4, IC5.pin3
  N20: SW1.5, IC5.pin14, R34.Pin_1
  N21: SW1.6, IC5.pin13, R31.Pin_1
  N22: SW1.7, IC5.pin12, R33.Pin_1
  N23: SW1.8, IC5.pin11, R32.Pin_1
  N24: SW2.1, IC8.pin6
  N25: SW2.2, IC8.pin5
  N26: SW2.3, IC8.pin4
  N27: SW2.4, IC8.pin3
  N28: SW2.5, IC8.pin14, R19.Pin_1
  N29: SW2.6, IC8.pin13, R20.Pin_1
  N30: SW2.7, IC8.pin12, R21.Pin_1
  N31: SW2.8, IC8.pin11, R22.Pin_1
  N32: SW3.1, IC9.pin6
  N33: SW3.2, IC9.pin5
  N34: SW3.3, IC9.pin4
  N35: SW3.4, IC9.pin3
  N36: SW3.5, IC9.pin14, R38.Pin_1
  N37: SW3.6, IC9.pin13, R35.Pin_1
  N38: SW3.7, IC9.pin12, R37.Pin_1
  N39: SW3.8, IC9.pin11, R36.Pin_1
  N40: IC2.pin1, IC10.pin1
  N41: IC2.pin2, IC10.pin2
  N42: IC2.pin6, IC10.pin3
  N43: IC2.pin7, IC10.pin15
  N44: IC2.pin8, IC7.pin8, R19.Pin_0, R20.Pin_0, R21.Pin_0, R22.Pin_0, R31.Pin_0, R32.Pin_0, R33.Pin_0, R34.Pin_0, R35.Pin_0, R36.Pin_0, R37.Pin_0, R38.Pin_0, IC10.pin8
  N45: IC7.pin1, IC10.pin5
  N46: IC7.pin2, IC10.pin6
  N47: IC7.pin6, IC10.pin7
  N48: IC7.pin7, IC10.pin4
  N49: IC7.pin11, R3.Pin_0
  N50: IC7.pin13, R8.Pin_1
  N51: IC7.pin14, R10.Pin_1
  N52: IC5.pin8, IC8.pin8, IC9.pin8, R15.Pin_1, R16.Pin_1, R17.Pin_1, R18.Pin_1, R23.Pin_1, R24.Pin_1, R25.Pin_1, R26.Pin_1, R27.Pin_1, R28.Pin_1, R29.Pin_1, R30.Pin_1, IC10.pin13
  N53: IC5.pin16, IC8.pin16, IC9.pin16

notes:
  Display Unit
  Input Blocks
  Num1
  Num2
  Operator
  PISO Shift Registers
  SIPO Shift Register
  Microcontroller
